// Logisim project ALU.circ as structural Verilog: 1 circuit, main circuit main
module main (
  input  A1,
  input  Cin,
  input  B1,
  input  A0,
  input  Cin_2,
  input  B0,
  input  [2:0] Select_Bits,
  output F1,
  output Cout,
  output Cout_2,
  output F0,
  output Cout_3,
  output Cout_4
);

  wire adder_1_out, adder_2_out, adder_3_out, adder_4_out, nand_1_out, nand_2_out, not_1_out, not_2_out,
       xor_1_out, xor_2_out;

  not not_1 (not_1_out, A1);
  not not_2 (not_2_out, A0);
  Adder #(.width(1)) adder_1 (.a(B0), .b(A0), .out(adder_1_out), .cin(Cin_2), .cout(Cout_3));
  xor xor_1 (xor_1_out, A0, B0);
  nand nand_1 (nand_1_out, A0, B0);
  Adder #(.width(1)) adder_2 (.a(A0), .b(1'b1), .out(adder_2_out), .cout(Cout_4));  // open: cin
  Adder #(.width(1)) adder_3 (.a(B1), .b(A1), .out(adder_3_out), .cin(Cin), .cout(Cout));
  xor xor_2 (xor_2_out, A1, B1);
  nand nand_2 (nand_2_out, A1, B1);
  Adder #(.width(1)) adder_4 (.a(A1), .b(1'b0), .out(adder_4_out), .cout(Cout_2));  // open: cin
  Multiplexer #(.select(3)) multiplexer_1 (
    .in0(not_1_out), .in1(adder_3_out), .in2(xor_2_out), .in3(nand_2_out), .in4(adder_4_out), .out(F1),
    .sel(Select_Bits));  // open: in5, in6, in7, en
  Multiplexer #(.select(3)) multiplexer_2 (
    .in0(not_2_out), .in1(adder_1_out), .in2(xor_1_out), .in3(nand_1_out), .in4(adder_2_out), .out(F0),
    .sel(Select_Bits));  // open: in5, in6, in7, en

  // Notes on the sheet:
  //   000 -> NOT_A
  //   001 -> ADD
  //   010 -> XOR
  //   011 -> NAND
  //   100 -> A+1
  //   NOT_A
  //   ADD
  //   XOR
  //   NAND
  //   A+1
  //   NOT_A
  //   ADD
  //   XOR
  //   NAND
  //   A+1
endmodule
